// Logisim project Rams.circ as structural Verilog: 15 circuits, main circuit main
module main (
  input  reset,
  output [15:0] out_2,
  output [15:0] out_3,
  output [15:0] out_4,
  output [15:0] out_5
);

  wire alu_16_bits_1_zero, alu_control_1_ainvert, alu_control_1_bnegate, ALU_OP_0, ALU_OP_1, ALU_OP_2,
       ALU_SRC, and_1_out, CLK, control_1_branch, JUMP, MEMREAD, MEMTREG, MEMWRITE, REGDEST, REGWRITE;
  wire [1:0] alu_control_1_operation;
  wire [3:0] multiplexer_1_out;
  wire [11:0] bitselector_1_out;
  wire [15:0] adder_1_out, bit_extender_2_out, JUMP_ADDR, multiplexer_3_out, multiplexer_4_out,
       multiplexer_5_out, PC_q, ram_1_data, registerfile_1_out_b;

  Clock clock_1 (.out(CLK));
  Register #(.width(16)) PC (.D(multiplexer_4_out), .Q(PC_q), .clk(CLK), .clr(reset));  // open: en
  ROM #(.addrWidth(16), .dataWidth(16)) rom_1 (.addr(PC_q), .data(out_3));  // open: sel
  Adder #(.width(16)) adder_1 (.a(16'h1), .b(PC_q), .out(adder_1_out));  // open: cin, cout
  assign JUMP_ADDR = {{4{1'b0}}, bitselector_1_out};  // Bit_Extender bit_extender_1
  BitSelector #(.width(16), .group(12)) bitselector_1 (.in(out_3), .out(bitselector_1_out), .sel(1'b0));
  CONTROL control_1 (
    .a(out_3[15]), .b(out_3[14]), .c(out_3[13]), .d(out_3[12]), .RegDest(REGDEST), .Branch(control_1_branch),
    .MemRead(MEMREAD), .MemToReg(MEMTREG), .ALUOp0(ALU_OP_0), .ALUOp1(ALU_OP_1), .ALUOp2(ALU_OP_2),
    .MemWrite(MEMWRITE), .ALUSrc(ALU_SRC), .RegWrite(REGWRITE), .Jump(JUMP));
  Multiplexer #(.width(4)) multiplexer_1 (
    .in0(out_3[7:4]), .in1(out_3[3:0]), .out(multiplexer_1_out), .sel(REGDEST));  // open: en
  assign bit_extender_2_out = {{12{1'b0}}, out_3[3:0]};  // Bit_Extender bit_extender_2
  RegisterFile registerfile_1 (
    .DATA(multiplexer_5_out), .OUT_A(out_2), .OUT_B(registerfile_1_out_b), .WRITE_REG(multiplexer_1_out),
    .REG_A(out_3[11:8]), .REG_B(out_3[7:4]), .CLK(CLK), .WRITE_DATA(REGWRITE));
  Multiplexer #(.width(16)) multiplexer_2 (
    .in0(registerfile_1_out_b), .in1(bit_extender_2_out), .out(out_5), .sel(ALU_SRC));  // open: en
  ALU_16_bits alu_16_bits_1 (
    .a(out_2), .b(out_5), .Result(out_4), .Zero(alu_16_bits_1_zero), .Operation(alu_control_1_operation),
    .Ainvert(alu_control_1_ainvert), .Bnegate(alu_control_1_bnegate));  // open: Overflow
  ALU_CONTROL alu_control_1 (
    .ALUOP0(ALU_OP_0), .ALUOP1(ALU_OP_1), .ALUOP2(ALU_OP_2), .BNEGATE(alu_control_1_bnegate),
    .AINVERT(alu_control_1_ainvert), .OPERATION(alu_control_1_operation));
  Multiplexer #(.width(16)) multiplexer_3 (
    .in0(adder_1_out), .in1(bit_extender_2_out), .out(multiplexer_3_out), .sel(and_1_out));  // open: en
  and and_1 (and_1_out, control_1_branch, alu_16_bits_1_zero);
  Multiplexer #(.width(16)) multiplexer_4 (
    .in0(multiplexer_3_out), .in1(JUMP_ADDR), .out(multiplexer_4_out), .sel(JUMP));  // open: en
  RAM #(.addrWidth(16), .dataWidth(16), .bus("separate")) ram_1 (
    .addr(out_4), .din(registerfile_1_out_b), .data(ram_1_data), .str(MEMWRITE), .clk(CLK));  // open: sel, ld, clr
  Multiplexer #(.width(16)) multiplexer_5 (
    .in0(out_4), .in1(ram_1_data), .out(multiplexer_5_out), .sel(MEMREAD));  // open: en

  // Notes on the sheet:
  //   contents of rom_1 (hex, n*v repeats v):
  //   9010 9020 9030 9064 761c 5140 8345 7059 403 9221 9111 f003 6034 f00c
endmodule

// ALU
module ALU_1_bit (
  input  a,
  input  Ainvert,
  input  b,
  input  CarryIn,
  input  [1:0] Operation,
  input  Binvert,
  input  Less,
  output Set,
  output Result,
  output CarryOut
);

  wire and_1_out, multiplexer_1_out, multiplexer_2_out, not_1_out, not_2_out, or_1_out;

  not not_1 (not_1_out, a);
  not not_2 (not_2_out, b);
  Multiplexer multiplexer_1 (.in0(a), .in1(not_1_out), .out(multiplexer_1_out), .sel(Ainvert));  // open: en
  Multiplexer multiplexer_2 (.in0(b), .in1(not_2_out), .out(multiplexer_2_out), .sel(Binvert));  // open: en
  and and_1 (and_1_out, multiplexer_1_out, multiplexer_2_out);
  or or_1 (or_1_out, multiplexer_1_out, multiplexer_2_out);
  Adder #(.width(1)) adder_1 (.a(multiplexer_1_out), .b(multiplexer_2_out), .out(Set), .cin(CarryIn), .cout(CarryOut));
  Multiplexer #(.select(2)) multiplexer_3 (
    .in0(and_1_out), .in1(or_1_out), .in2(Set), .in3(Less), .out(Result), .sel(Operation));  // open: en
endmodule

module ALU_16_bits (
  input  Ainvert,
  input  Bnegate,
  input  [1:0] Operation,
  input  [15:0] a,
  input  [15:0] b,
  output [15:0] Result,
  output Zero,
  output Overflow
);

  wire alu_1_bit_1_carryout, alu_1_bit_2_carryout, alu_1_bit_3_carryout, alu_1_bit_4_carryout,
       alu_1_bit_5_carryout, alu_1_bit_6_carryout, alu_1_bit_7_carryout, alu_1_bit_8_carryout,
       alu_1_bit_9_carryout, alu_1_bit_10_carryout, alu_1_bit_11_carryout, alu_1_bit_12_carryout,
       alu_1_bit_13_carryout, alu_1_bit_14_carryout, alu_1_bit_15_carryout, alu_1_bit_16_set, or_1_out;

  ALU_1_bit alu_1_bit_1 (
    .a(a[0]), .b(b[0]), .Less(alu_1_bit_16_set), .Ainvert(Ainvert), .Result(Result[0]), .CarryIn(Bnegate),
    .Operation(Operation), .Binvert(Bnegate), .CarryOut(alu_1_bit_1_carryout));  // open: Set
  ALU_1_bit alu_1_bit_2 (
    .a(a[1]), .b(b[1]), .Less(1'b0), .Ainvert(Ainvert), .Result(Result[1]), .CarryIn(alu_1_bit_1_carryout),
    .Operation(Operation), .Binvert(Bnegate), .CarryOut(alu_1_bit_2_carryout));  // open: Set
  ALU_1_bit alu_1_bit_3 (
    .a(a[2]), .b(b[2]), .Less(1'b0), .Ainvert(Ainvert), .Result(Result[2]), .CarryIn(alu_1_bit_2_carryout),
    .Operation(Operation), .Binvert(Bnegate), .CarryOut(alu_1_bit_3_carryout));  // open: Set
  ALU_1_bit alu_1_bit_4 (
    .a(a[3]), .b(b[3]), .Less(1'b0), .Ainvert(Ainvert), .Result(Result[3]), .CarryIn(alu_1_bit_3_carryout),
    .Operation(Operation), .Binvert(Bnegate), .CarryOut(alu_1_bit_4_carryout));  // open: Set
  ALU_1_bit alu_1_bit_5 (
    .a(a[4]), .b(b[4]), .Less(1'b0), .Ainvert(Ainvert), .Result(Result[4]), .CarryIn(alu_1_bit_4_carryout),
    .Operation(Operation), .Binvert(Bnegate), .CarryOut(alu_1_bit_5_carryout));  // open: Set
  ALU_1_bit alu_1_bit_6 (
    .a(a[5]), .b(b[5]), .Less(1'b0), .Ainvert(Ainvert), .Result(Result[5]), .CarryIn(alu_1_bit_5_carryout),
    .Operation(Operation), .Binvert(Bnegate), .CarryOut(alu_1_bit_6_carryout));  // open: Set
  ALU_1_bit alu_1_bit_7 (
    .a(a[6]), .b(b[6]), .Less(1'b0), .Ainvert(Ainvert), .Result(Result[6]), .CarryIn(alu_1_bit_6_carryout),
    .Operation(Operation), .Binvert(Bnegate), .CarryOut(alu_1_bit_7_carryout));  // open: Set
  ALU_1_bit alu_1_bit_8 (
    .a(a[7]), .b(b[7]), .Less(1'b0), .Ainvert(Ainvert), .Result(Result[7]), .CarryIn(alu_1_bit_7_carryout),
    .Operation(Operation), .Binvert(Bnegate), .CarryOut(alu_1_bit_8_carryout));  // open: Set
  ALU_1_bit alu_1_bit_9 (
    .a(a[8]), .b(b[8]), .Less(1'b0), .Ainvert(Ainvert), .Result(Result[8]), .CarryIn(alu_1_bit_8_carryout),
    .Operation(Operation), .Binvert(Bnegate), .CarryOut(alu_1_bit_9_carryout));  // open: Set
  ALU_1_bit alu_1_bit_10 (
    .a(a[9]), .b(b[9]), .Less(1'b0), .Ainvert(Ainvert), .Result(Result[9]), .CarryIn(alu_1_bit_9_carryout),
    .Operation(Operation), .Binvert(Bnegate), .CarryOut(alu_1_bit_10_carryout));  // open: Set
  ALU_1_bit alu_1_bit_11 (
    .a(a[10]), .b(b[10]), .Less(1'b0), .Ainvert(Ainvert), .Result(Result[10]),
    .CarryIn(alu_1_bit_10_carryout), .Operation(Operation), .Binvert(Bnegate),
    .CarryOut(alu_1_bit_11_carryout));  // open: Set
  ALU_1_bit alu_1_bit_12 (
    .a(a[11]), .b(b[11]), .Less(1'b0), .Ainvert(Ainvert), .Result(Result[11]),
    .CarryIn(alu_1_bit_11_carryout), .Operation(Operation), .Binvert(Bnegate),
    .CarryOut(alu_1_bit_12_carryout));  // open: Set
  ALU_1_bit alu_1_bit_13 (
    .a(a[12]), .b(b[12]), .Less(1'b0), .Ainvert(Ainvert), .Result(Result[12]),
    .CarryIn(alu_1_bit_12_carryout), .Operation(Operation), .Binvert(Bnegate),
    .CarryOut(alu_1_bit_13_carryout));  // open: Set
  ALU_1_bit alu_1_bit_14 (
    .a(a[13]), .b(b[13]), .Less(1'b0), .Ainvert(Ainvert), .Result(Result[13]),
    .CarryIn(alu_1_bit_13_carryout), .Operation(Operation), .Binvert(Bnegate),
    .CarryOut(alu_1_bit_14_carryout));  // open: Set
  ALU_1_bit alu_1_bit_15 (
    .a(a[14]), .b(b[14]), .Less(1'b0), .Ainvert(Ainvert), .Result(Result[14]),
    .CarryIn(alu_1_bit_14_carryout), .Operation(Operation), .Binvert(Bnegate),
    .CarryOut(alu_1_bit_15_carryout));  // open: Set
  ALU_1_bit alu_1_bit_16 (
    .a(a[15]), .b(b[15]), .Less(1'b0), .Ainvert(Ainvert), .Result(Result[15]),
    .CarryIn(alu_1_bit_15_carryout), .Operation(Operation), .Binvert(Bnegate), .Set(alu_1_bit_16_set),
    .CarryOut(Overflow));
  not not_1 (Zero, or_1_out);
  or or_1 (or_1_out, Result[0], Result[1], Result[2], Result[3], Result[4], Result[5], Result[6], Result[7], Result[8], Result[9], Result[10], Result[11], Result[12], Result[13], Result[14], Result[15]);
endmodule

module RegisterFile (
  input  [15:0] DATA,
  input  [3:0] REG_A,
  input  CLK,
  input  WRITE_DATA,
  input  [3:0] WRITE_REG,
  input  [3:0] REG_B,
  output [15:0] OUT_A,
  output [15:0] OUT_B
);

  wire demultiplexer_1_out1, demultiplexer_1_out2, demultiplexer_1_out3, demultiplexer_1_out4,
       demultiplexer_1_out5, demultiplexer_1_out6, demultiplexer_1_out7, demultiplexer_1_out8,
       demultiplexer_1_out9, demultiplexer_1_out10, demultiplexer_1_out11, demultiplexer_1_out12,
       demultiplexer_1_out13, demultiplexer_1_out14, demultiplexer_1_out15;
  wire [15:0] register_1_q, register_2_q, register_3_q, register_4_q, register_5_q, register_6_q,
       register_7_q, S0_q, S1_q, S2_q, S3_q, T0_q, T1_q, T2_q, T3_q, ZERO_q;

  Demultiplexer #(.select(4)) demultiplexer_1 (
    .out1(demultiplexer_1_out1), .out2(demultiplexer_1_out2), .out3(demultiplexer_1_out3),
    .out4(demultiplexer_1_out4), .out5(demultiplexer_1_out5), .out6(demultiplexer_1_out6),
    .out7(demultiplexer_1_out7), .out8(demultiplexer_1_out8), .out9(demultiplexer_1_out9),
    .out10(demultiplexer_1_out10), .out11(demultiplexer_1_out11), .out12(demultiplexer_1_out12),
    .out13(demultiplexer_1_out13), .out14(demultiplexer_1_out14), .out15(demultiplexer_1_out15),
    .in(WRITE_DATA), .sel(WRITE_REG));  // open: out0, en
  Register #(.width(16)) ZERO (.Q(ZERO_q), .clk(CLK));  // open: D, en, clr
  Register #(.width(16)) T0 (.D(DATA), .en(demultiplexer_1_out1), .Q(T0_q), .clk(CLK));  // open: clr
  Register #(.width(16)) T1 (.D(DATA), .en(demultiplexer_1_out2), .Q(T1_q), .clk(CLK));  // open: clr
  Register #(.width(16)) T2 (.D(DATA), .en(demultiplexer_1_out3), .Q(T2_q), .clk(CLK));  // open: clr
  Register #(.width(16)) T3 (.D(DATA), .en(demultiplexer_1_out4), .Q(T3_q), .clk(CLK));  // open: clr
  Register #(.width(16)) S0 (.D(DATA), .en(demultiplexer_1_out5), .Q(S0_q), .clk(CLK));  // open: clr
  Register #(.width(16)) S1 (.D(DATA), .en(demultiplexer_1_out6), .Q(S1_q), .clk(CLK));  // open: clr
  Register #(.width(16)) S2 (.D(DATA), .en(demultiplexer_1_out7), .Q(S2_q), .clk(CLK));  // open: clr
  Register #(.width(16)) S3 (.D(DATA), .en(demultiplexer_1_out8), .Q(S3_q), .clk(CLK));  // open: clr
  Register #(.width(16)) register_1 (.D(DATA), .en(demultiplexer_1_out9), .Q(register_1_q), .clk(CLK));  // open: clr
  Register #(.width(16)) register_2 (.D(DATA), .en(demultiplexer_1_out10), .Q(register_2_q), .clk(CLK));  // open: clr
  Register #(.width(16)) register_3 (.D(DATA), .en(demultiplexer_1_out11), .Q(register_3_q), .clk(CLK));  // open: clr
  Register #(.width(16)) register_4 (.D(DATA), .en(demultiplexer_1_out12), .Q(register_4_q), .clk(CLK));  // open: clr
  Register #(.width(16)) register_5 (.D(DATA), .en(demultiplexer_1_out13), .Q(register_5_q), .clk(CLK));  // open: clr
  Register #(.width(16)) register_6 (.D(DATA), .en(demultiplexer_1_out14), .Q(register_6_q), .clk(CLK));  // open: clr
  Register #(.width(16)) register_7 (.D(DATA), .en(demultiplexer_1_out15), .Q(register_7_q), .clk(CLK));  // open: clr
  Multiplexer #(.select(4), .width(16)) multiplexer_1 (
    .in0(ZERO_q), .in1(T0_q), .in2(T1_q), .in3(T2_q), .in4(T3_q), .in5(S0_q), .in6(S1_q), .in7(S2_q),
    .in8(S3_q), .in9(register_1_q), .in10(register_2_q), .in11(register_3_q), .in12(register_4_q),
    .in13(register_5_q), .in14(register_6_q), .in15(register_7_q), .out(OUT_A), .sel(REG_A));  // open: en
  Multiplexer #(.select(4), .width(16)) multiplexer_2 (
    .in0(ZERO_q), .in1(T0_q), .in2(T1_q), .in3(T2_q), .in4(T3_q), .in5(S0_q), .in6(S1_q), .in7(S2_q),
    .in8(S3_q), .in9(register_1_q), .in10(register_2_q), .in11(register_3_q), .in12(register_4_q),
    .in13(register_5_q), .in14(register_6_q), .in15(register_7_q), .out(OUT_B), .sel(REG_B));  // open: en
endmodule

module k (
  input  in_1,
  input  in_2,
  input  in_3,
  input  in_4,
  output RegDest,
  output Branch,
  output MemRead,
  output MemToReg,
  output ALUOp0,
  output ALUOp1,
  output ALUOp2,
  output MemWrite,
  output ALUSrc,
  output RegWrite
);
endmodule

module Control_alpha (
  input  a,
  input  b,
  input  c,
  input  d,
  input  e,
  input  f,
  output RegDest,
  output Branch,
  output MemRead,
  output MemToReg,
  output ALUOp0,
  output ALUOp1,
  output ALUOp1_2,
  output MemWrite,
  output ALUSrc,
  output RegWrite,
  output Jump
);

  wire and_2_out, and_3_out, and_4_out, and_5_out, and_6_out, and_7_out, and_8_out, and_9_out, and_10_out,
       and_11_out, and_12_out, and_13_out, and_14_out, and_15_out, and_16_out, and_17_out, and_18_out,
       and_19_out, and_20_out, and_21_out, and_22_out, and_23_out, and_24_out, and_25_out, and_26_out,
       and_27_out, and_28_out, and_29_out, and_30_out, and_31_out, and_32_out, and_33_out, and_34_out,
       and_35_out, not_1_out, not_2_out, not_3_out, not_4_out, not_5_out, not_6_out, not_7_out, not_8_out,
       not_9_out, not_10_out, not_11_out, not_12_out, not_13_out, not_14_out, not_15_out, not_16_out,
       not_17_out, not_18_out, not_19_out, not_20_out, not_21_out, not_22_out, not_23_out, not_24_out,
       not_25_out, not_26_out, not_27_out, not_28_out, not_29_out, not_30_out, not_31_out, not_32_out,
       not_33_out, not_34_out, not_35_out, not_36_out, not_37_out, not_38_out, not_39_out, not_40_out,
       not_41_out, not_42_out, not_43_out, not_44_out, not_45_out, not_46_out, not_47_out, not_48_out,
       not_49_out, not_50_out, not_51_out, not_52_out, not_53_out, not_54_out, not_55_out, not_56_out,
       not_57_out, not_58_out, not_59_out;

  not not_1 (not_1_out, d);
  not not_2 (not_2_out, c);
  not not_3 (not_3_out, c);
  not not_4 (not_4_out, e);
  not not_5 (not_5_out, c);
  not not_6 (not_6_out, c);
  not not_7 (not_7_out, e);
  not not_8 (not_8_out, f);
  not not_9 (not_9_out, c);
  not not_10 (not_10_out, c);
  not not_11 (not_11_out, e);
  not not_12 (not_12_out, f);
  not not_13 (not_13_out, d);
  not not_14 (not_14_out, e);
  not not_15 (not_15_out, c);
  not not_16 (not_16_out, e);
  not not_17 (not_17_out, f);
  not not_18 (not_18_out, c);
  not not_19 (not_19_out, e);
  not not_20 (not_20_out, f);
  not not_21 (not_21_out, c);
  not not_22 (not_22_out, c);
  not not_23 (not_23_out, e);
  not not_24 (not_24_out, f);
  not not_25 (not_25_out, d);
  not not_26 (not_26_out, e);
  not not_27 (not_27_out, c);
  not not_28 (not_28_out, e);
  not not_29 (not_29_out, f);
  not not_30 (not_30_out, c);
  not not_31 (not_31_out, e);
  not not_32 (not_32_out, f);
  or or_1 (ALUOp1, f, e, d, c, b, a);
  not not_33 (not_33_out, e);
  not not_34 (not_34_out, c);
  not not_35 (not_35_out, d);
  not not_36 (not_36_out, f);
  not not_37 (not_37_out, c);
  not not_38 (not_38_out, e);
  not not_39 (not_39_out, c);
  not not_40 (not_40_out, d);
  not not_41 (not_41_out, f);
  not not_42 (not_42_out, c);
  not not_43 (not_43_out, d);
  not not_44 (not_44_out, f);
  not not_45 (not_45_out, c);
  not not_46 (not_46_out, d);
  not not_47 (not_47_out, d);
  not not_48 (not_48_out, e);
  not not_49 (not_49_out, c);
  not not_50 (not_50_out, d);
  not not_51 (not_51_out, f);
  not not_52 (not_52_out, e);
  not not_53 (not_53_out, f);
  not not_54 (not_54_out, d);
  not not_55 (not_55_out, c);
  not not_56 (not_56_out, f);
  not not_57 (not_57_out, c);
  not not_58 (not_58_out, e);
  not not_59 (not_59_out, d);
  and and_1 (Jump, c, e, f);
  and and_2 (and_2_out, not_1_out, f);
  and and_3 (and_3_out, not_2_out, e);
  and and_4 (and_4_out, not_3_out, d);
  and and_5 (and_5_out, c, not_4_out);
  and and_6 (and_6_out, b, not_5_out);
  and and_7 (and_7_out, a, not_6_out);
  and and_8 (and_8_out, c, not_7_out, not_8_out);
  and and_9 (and_9_out, c, d, e);
  and and_10 (and_10_out, not_9_out, e, f);
  and and_11 (and_11_out, not_10_out, d, not_11_out, not_12_out);
  and and_12 (and_12_out, c, not_13_out, not_14_out, f);
  and and_13 (and_13_out, b, not_15_out, not_16_out, not_17_out);
  and and_14 (and_14_out, a, not_18_out, not_19_out, not_20_out);
  and and_15 (and_15_out, not_21_out, e, f);
  and and_16 (and_16_out, not_22_out, d, not_23_out, not_24_out);
  and and_17 (and_17_out, c, not_25_out, not_26_out, f);
  and and_18 (and_18_out, b, not_27_out, not_28_out, not_29_out);
  and and_19 (and_19_out, a, not_30_out, not_31_out, not_32_out);
  and and_20 (and_20_out, c, e, f);
  and and_21 (and_21_out, c, d, not_33_out);
  and and_22 (and_22_out, not_34_out, not_35_out, e, not_36_out);
  and and_23 (and_23_out, not_37_out, d, not_38_out, f);
  and and_24 (and_24_out, b, not_39_out, not_40_out, not_41_out);
  and and_25 (and_25_out, a, not_42_out, not_43_out, not_44_out);
  and and_26 (and_26_out, not_45_out, not_46_out, f);
  and and_27 (and_27_out, not_47_out, not_48_out, f);
  and and_28 (and_28_out, not_49_out, d, e);
  and and_29 (and_29_out, c, not_50_out, e, not_51_out);
  and and_30 (and_30_out, c, d, not_52_out, not_53_out);
  and and_31 (and_31_out, not_54_out, f);
  and and_32 (and_32_out, not_55_out, d, not_56_out);
  and and_33 (and_33_out, not_57_out, d, e);
  and and_34 (and_34_out, c, not_58_out, f);
  and and_35 (and_35_out, c, not_59_out, e);
  or or_2 (RegDest, and_2_out, and_3_out, and_4_out, and_5_out, and_6_out, and_7_out);
  or or_3 (Branch, and_8_out, and_9_out);
  or or_4 (MemRead, and_10_out, and_11_out, and_12_out, and_13_out, and_14_out);
  or or_5 (MemToReg, and_15_out, and_16_out, and_17_out, and_18_out, and_19_out);
  or or_6 (ALUOp1_2, and_20_out, and_21_out);
  or or_7 (MemWrite, and_22_out, and_23_out, and_24_out, and_25_out);
  or or_8 (ALUSrc, and_26_out, and_27_out, and_28_out, and_29_out, and_30_out);
  or or_9 (RegWrite, and_31_out, and_32_out, and_33_out, and_34_out, and_35_out);
endmodule

module test (
  input  reset,
  input  reset_2,
  output [15:0] out_3,
  output [15:0] out_4,
  output [15:0] out_5,
  output [15:0] out_6
);

  wire alu_16_bits_1_zero, alu_control_1_ainvert, alu_control_1_bnegate, ALU_OP_0, ALU_OP_1, ALU_OP_2,
       ALU_SRC, and_1_out, CLK, control_beta_1_branch, control_beta_1_jump, MEMREAD, MEMTREG, MEMWRITE,
       REGDEST, REGWRITE, ROM;
  wire [1:0] alu_control_1_operation;
  wire [1:1] multiplexer_1_out;
  wire [2:0] multiplexer_2_out;
  wire [15:0] adder_1_out, bit_extender_1_out, multiplexer_4_out, program_counter_1_address, ram_1_data,
       registerfile_1_p1, registerfile_1_p8;

  Clock clock_1 (.out(CLK));
  PROGRAM_COUNTER program_counter_1 (
    .INPUT(multiplexer_4_out), .CLK(CLK), .ADDRESS(program_counter_1_address));  // open: ADDRESS_2
  ROM #(.addrWidth(16), .dataWidth(16)) rom_1 (.addr(program_counter_1_address), .data(out_4));  // open: sel
  Adder #(.width(16)) adder_1 (.a(16'h1), .b(program_counter_1_address), .out(adder_1_out));  // open: cin, cout
  Multiplexer multiplexer_1 (.in0(out_4[8]), .in1(reset_2), .out(multiplexer_1_out[1]), .sel(reset_2));  // open: en
  CONTROL_BETA control_beta_1 (
    .a(out_4[15]), .b(out_4[14]), .c(out_4[13]), .d(out_4[12]), .e(out_4[11]), .f(out_4[10]),
    .RegDest(REGDEST), .Branch(control_beta_1_branch), .MemRead(MEMREAD), .MemToReg(MEMTREG),
    .ALUOp0(ALU_OP_0), .ALUOp1(ALU_OP_1), .ALUOp12(ALU_OP_2), .MemWrite(MEMWRITE), .ALUSrc(ALU_SRC),
    .RegWrite(REGWRITE), .Jump(control_beta_1_jump), .ROM(ROM));
  Multiplexer #(.width(3)) multiplexer_2 (
    .in0({out_4[4], out_4[5], out_4[6]}), .in1({out_4[1], out_4[2], out_4[3]}), .out(multiplexer_2_out),
    .sel(REGDEST));  // open: en
  assign bit_extender_1_out = {{8{1'b0}}, out_4[7:0]};  // Bit_Extender bit_extender_1
  // RegisterFile registerfile_1: pin names not known; wires that end beside it: registerfile_1_p1, {out_4[7], multiplexer_1_out[1], out_4[9]}, {out_4[4], out_4[5], out_4[6]}, multiplexer_2_out, REGWRITE, CLK, out_3, registerfile_1_p8
  Multiplexer #(.width(16)) multiplexer_3 (
    .in0(registerfile_1_p8), .in1(bit_extender_1_out), .out(out_6), .sel(ALU_SRC));  // open: en
  ALU_16_bits alu_16_bits_1 (
    .a(out_3), .b(out_6), .Result(out_5), .Zero(alu_16_bits_1_zero), .Operation(alu_control_1_operation),
    .Ainvert(alu_control_1_ainvert), .Bnegate(alu_control_1_bnegate));  // open: Overflow
  ALU_CONTROL alu_control_1 (
    .ALUOP0(ALU_OP_0), .ALUOP1(ALU_OP_1), .ALUOP2(ALU_OP_2), .BNEGATE(alu_control_1_bnegate),
    .AINVERT(alu_control_1_ainvert), .OPERATION(alu_control_1_operation));
  Multiplexer #(.width(16)) multiplexer_4 (
    .in0(adder_1_out), .in1(bit_extender_1_out), .out(multiplexer_4_out), .sel(and_1_out));  // open: en
  and and_1 (and_1_out, control_beta_1_branch, alu_16_bits_1_zero);
  RAM #(.addrWidth(16), .dataWidth(16), .bus("separate")) ram_1 (.data(ram_1_data));  // open: addr, din, str, sel, clk, ld, clr
  Multiplexer #(.width(16)) multiplexer_5 (
    .in0(out_5), .in1(ram_1_data), .out(registerfile_1_p1), .sel(MEMREAD));  // open: en

  // Notes on the sheet:
  //   contents of rom_1 (hex, n*v repeats v):
  //   1904 3800
endmodule

module Instructions_Handler (
  input  [15:0] NEXT,
  input  reset,
  input  CLK,
  output [15:0] INST
);

  wire bitselector_1_out, not_1_out;
  wire [1:0] adder_1_out, INIT_q;
  wire [15:0] multiplexer_1_out, NEXT_INST_q;

  Adder #(.width(2)) adder_1 (.a(INIT_q), .b(2'b01), .out(adder_1_out));  // open: cin, cout
  BitSelector #(.width(2)) bitselector_1 (.in(INIT_q), .out(bitselector_1_out), .sel(1'b0));
  Register #(.width(16)) NEXT_INST (.D(NEXT), .en(bitselector_1_out), .Q(NEXT_INST_q), .clk(CLK), .clr(reset));
  not not_1 (not_1_out, bitselector_1_out);
  Multiplexer #(.width(16)) multiplexer_1 (
    .in0(NEXT), .in1(NEXT_INST_q), .out(multiplexer_1_out), .sel(bitselector_1_out));  // open: en
  Register #(.width(2)) INIT (.D(adder_1_out), .en(not_1_out), .Q(INIT_q), .clk(CLK), .clr(reset));
  Register #(.width(16)) INSTRUCTION (.D(multiplexer_1_out), .Q(INST), .clk(CLK), .clr(reset));  // open: en
endmodule

module ALU_CONTROL (
  input  ALUOP0,
  input  ALUOP1,
  input  ALUOP2,
  output [1:0] OPERATION,
  output BNEGATE,
  output AINVERT
);

  wire and_1_out, and_2_out, and_3_out, and_4_out, not_1_out, not_2_out, not_3_out, not_4_out;

  and and_1 (and_1_out, ALUOP1, ALUOP2);
  not not_1 (not_1_out, ALUOP1);
  not not_2 (not_2_out, ALUOP2);
  not not_3 (not_3_out, ALUOP2);
  not not_4 (not_4_out, ALUOP2);
  or or_1 (OPERATION[1], and_1_out, ALUOP0);
  and and_2 (and_2_out, not_1_out, ALUOP2);
  and and_3 (and_3_out, ALUOP1, not_2_out);
  and and_4 (and_4_out, ALUOP1, not_3_out);
  and and_5 (AINVERT, ALUOP1, not_4_out);
  or or_2 (OPERATION[0], and_2_out, and_3_out);
  or or_3 (BNEGATE, and_4_out, ALUOP0);
endmodule

module test_alu (
  input  ALUOP0,
  input  ALUOP1,
  input  ALUOP2,
  output op1,
  output op2,
  output BNEGATE,
  output AINVERT
);

  wire and_1_out, and_2_out, and_3_out, and_4_out, not_1_out, not_2_out, not_3_out, not_4_out;

  and and_1 (and_1_out, ALUOP1, ALUOP2);
  not not_1 (not_1_out, ALUOP1);
  not not_2 (not_2_out, ALUOP2);
  not not_3 (not_3_out, ALUOP2);
  not not_4 (not_4_out, ALUOP2);
  or or_1 (op1, and_1_out, ALUOP0);
  and and_2 (and_2_out, not_1_out, ALUOP2);
  and and_3 (and_3_out, ALUOP1, not_2_out);
  and and_4 (and_4_out, ALUOP1, not_3_out);
  and and_5 (AINVERT, ALUOP1, not_4_out);
  or or_2 (op2, and_2_out, and_3_out);
  or or_3 (BNEGATE, and_4_out, ALUOP0);
endmodule

module CONTROL_BETA (
  input  a,
  input  b,
  input  c,
  input  d,
  input  e,
  input  f,
  output RegDest,
  output Branch,
  output MemRead,
  output MemToReg,
  output ALUOp0,
  output ALUOp1,
  output ALUOp12,
  output MemWrite,
  output ALUSrc,
  output RegWrite,
  output Jump,
  output ROM
);

  wire and_2_out, and_3_out, and_4_out, and_5_out, and_6_out, and_7_out, and_8_out, and_9_out, and_10_out,
       and_11_out, and_12_out, and_13_out, and_14_out, and_15_out, and_16_out, and_17_out, and_18_out,
       and_19_out, and_20_out, and_21_out, and_22_out, and_23_out, and_24_out, and_25_out, and_26_out,
       and_27_out, and_28_out, and_29_out, and_30_out, and_31_out, and_32_out, and_33_out, and_34_out,
       and_35_out, and_36_out, and_37_out, and_38_out, and_39_out, not_1_out, not_2_out, not_3_out,
       not_4_out, not_5_out, not_6_out, not_7_out, not_8_out, not_9_out, not_10_out, not_11_out, not_12_out,
       not_13_out, not_14_out, not_15_out, not_16_out, not_17_out, not_18_out, not_19_out, not_20_out,
       not_21_out, not_22_out, not_23_out, not_24_out, not_25_out, not_26_out, not_27_out, not_28_out,
       not_29_out, not_30_out, not_31_out, not_32_out, not_33_out, not_34_out, not_35_out, not_36_out,
       not_37_out, not_38_out, not_39_out, not_40_out, not_41_out, not_42_out, not_43_out, not_44_out,
       not_45_out, not_46_out, not_47_out, not_48_out, not_49_out, not_50_out, not_51_out, not_52_out,
       not_53_out, not_54_out, not_55_out, not_56_out, not_57_out, not_58_out, not_59_out, not_60_out,
       not_61_out, not_62_out, not_63_out, not_64_out, not_65_out, not_66_out, not_67_out;

  not not_1 (not_1_out, d);
  not not_2 (not_2_out, c);
  not not_3 (not_3_out, c);
  not not_4 (not_4_out, e);
  not not_5 (not_5_out, c);
  not not_6 (not_6_out, c);
  not not_7 (not_7_out, e);
  not not_8 (not_8_out, f);
  not not_9 (not_9_out, c);
  not not_10 (not_10_out, c);
  not not_11 (not_11_out, e);
  not not_12 (not_12_out, f);
  not not_13 (not_13_out, d);
  not not_14 (not_14_out, e);
  not not_15 (not_15_out, c);
  not not_16 (not_16_out, e);
  not not_17 (not_17_out, f);
  not not_18 (not_18_out, c);
  not not_19 (not_19_out, e);
  not not_20 (not_20_out, f);
  not not_21 (not_21_out, c);
  not not_22 (not_22_out, c);
  not not_23 (not_23_out, e);
  not not_24 (not_24_out, f);
  not not_25 (not_25_out, d);
  not not_26 (not_26_out, e);
  not not_27 (not_27_out, c);
  not not_28 (not_28_out, e);
  not not_29 (not_29_out, f);
  not not_30 (not_30_out, c);
  not not_31 (not_31_out, e);
  not not_32 (not_32_out, f);
  not not_33 (not_33_out, e);
  not not_34 (not_34_out, d);
  not not_35 (not_35_out, e);
  not not_36 (not_36_out, f);
  not not_37 (not_37_out, d);
  not not_38 (not_38_out, e);
  not not_39 (not_39_out, f);
  not not_40 (not_40_out, c);
  not not_41 (not_41_out, d);
  not not_42 (not_42_out, f);
  not not_43 (not_43_out, c);
  not not_44 (not_44_out, e);
  not not_45 (not_45_out, c);
  not not_46 (not_46_out, d);
  not not_47 (not_47_out, f);
  not not_48 (not_48_out, c);
  not not_49 (not_49_out, d);
  not not_50 (not_50_out, f);
  not not_51 (not_51_out, c);
  not not_52 (not_52_out, d);
  not not_53 (not_53_out, d);
  not not_54 (not_54_out, e);
  not not_55 (not_55_out, c);
  not not_56 (not_56_out, d);
  not not_57 (not_57_out, f);
  not not_58 (not_58_out, e);
  not not_59 (not_59_out, f);
  not not_60 (not_60_out, d);
  not not_61 (not_61_out, c);
  not not_62 (not_62_out, f);
  not not_63 (not_63_out, c);
  not not_64 (not_64_out, e);
  not not_65 (not_65_out, d);
  and and_1 (Jump, c, e, f);
  and and_2 (and_2_out, not_1_out, f);
  and and_3 (and_3_out, not_2_out, e);
  and and_4 (and_4_out, not_3_out, d);
  and and_5 (and_5_out, c, not_4_out);
  and and_6 (and_6_out, b, not_5_out);
  and and_7 (and_7_out, a, not_6_out);
  and and_8 (and_8_out, c, not_7_out, not_8_out);
  and and_9 (and_9_out, c, d, e);
  and and_10 (and_10_out, not_9_out, e, f);
  and and_11 (and_11_out, not_10_out, d, not_11_out, not_12_out);
  and and_12 (and_12_out, c, not_13_out, not_14_out, f);
  and and_13 (and_13_out, b, not_15_out, not_16_out, not_17_out);
  and and_14 (and_14_out, a, not_18_out, not_19_out, not_20_out);
  and and_15 (and_15_out, not_21_out, e, f);
  and and_16 (and_16_out, not_22_out, d, not_23_out, not_24_out);
  and and_17 (and_17_out, c, not_25_out, not_26_out, f);
  and and_18 (and_18_out, b, not_27_out, not_28_out, not_29_out);
  and and_19 (and_19_out, a, not_30_out, not_31_out, not_32_out);
  and and_20 (and_20_out, c, e, f);
  and and_21 (and_21_out, c, d, not_33_out);
  not not_66 (not_66_out, c);
  and and_22 (and_22_out, not_34_out, not_35_out);
  and and_23 (and_23_out, e, not_36_out);
  not not_67 (not_67_out, c);
  and and_24 (and_24_out, not_37_out, not_38_out);
  and and_25 (and_25_out, e, not_39_out);
  and and_26 (and_26_out, not_40_out, not_41_out, e, not_42_out);
  and and_27 (and_27_out, not_43_out, d, not_44_out, f);
  and and_28 (and_28_out, b, not_45_out, not_46_out, not_47_out);
  and and_29 (and_29_out, a, not_48_out, not_49_out, not_50_out);
  and and_30 (and_30_out, not_51_out, not_52_out, f);
  and and_31 (and_31_out, not_53_out, not_54_out, f);
  and and_32 (and_32_out, not_55_out, d, e);
  and and_33 (and_33_out, c, not_56_out, e, not_57_out);
  and and_34 (and_34_out, c, d, not_58_out, not_59_out);
  and and_35 (and_35_out, not_60_out, f);
  and and_36 (and_36_out, not_61_out, d, not_62_out);
  and and_37 (and_37_out, not_63_out, d, e);
  and and_38 (and_38_out, c, not_64_out, f);
  and and_39 (and_39_out, c, not_65_out, e);
  or or_1 (RegDest, and_2_out, and_3_out, and_4_out, and_5_out, and_6_out, and_7_out);
  or or_2 (Branch, and_8_out, and_9_out);
  or or_3 (MemRead, and_10_out, and_11_out, and_12_out, and_13_out, and_14_out);
  or or_4 (MemToReg, and_15_out, and_16_out, and_17_out, and_18_out, and_19_out);
  or or_5 (ALUOp0, and_20_out, and_21_out);
  or or_6 (ALUOp1, not_66_out, and_22_out, and_23_out);
  or or_7 (ALUOp12, not_67_out, and_24_out, and_25_out);
  or or_8 (MemWrite, and_26_out, and_27_out, and_28_out, and_29_out);
  or or_9 (ALUSrc, and_30_out, and_31_out, and_32_out, and_33_out, and_34_out);
  or or_10 (RegWrite, and_35_out, and_36_out, and_37_out, and_38_out, and_39_out);

  assign ROM = a;
endmodule

module mini_tests (
  input  in_1,
  input  [15:0] in_2,
  input  in_3,
  input  [2:0] in_4,
  input  [2:0] in_5,
  input  [2:0] in_6,
  input  in_7,
  input  in_8,
  output out_9,
  output [15:0] out_10
);

  wire and_1_out, not_1_out;

  // RegisterFile registerfile_1: pin names not known; wires that end beside it: in_2, in_4, in_5, in_6, in_8, out_10
  not not_1 (not_1_out, in_3);
  and and_1 (and_1_out, in_3, not_1_out);
  Register #(.width(1)) register_1 (.D(in_1), .Q(out_9), .clk(and_1_out));  // open: en, clr
endmodule

module PROGRAM_COUNTER (
  input  [15:0] INPUT,
  input  CLK,
  output [15:0] ADDRESS,
  output [1:0] ADDRESS_2
);

  wire counter_1_carry;

  Register #(.width(16)) PC (.D(INPUT), .Q(ADDRESS), .clk(counter_1_carry));  // open: en, clr
  Counter #(.width(2), .max('h3)) counter_1 (
    .D(2'b11), .count(1'b1), .Q(ADDRESS_2), .carry(counter_1_carry), .clk(CLK), .clr(counter_1_carry));  // open: load
endmodule

module CONTROL_BETA2 (
  input  a,
  input  b,
  input  c,
  input  d,
  output RegDest,
  output Branch,
  output MemRead,
  output MemToReg,
  output ALUOp0,
  output ALUOp1,
  output ALUOp2,
  output MemWrite,
  output ALUSrc,
  output RegWrite,
  output Jump
);

  wire and_1_out, and_2_out, and_3_out, and_4_out, and_5_out, and_6_out, and_7_out, and_8_out, and_9_out,
       and_10_out, and_11_out, and_12_out, and_13_out, and_14_out, and_15_out, and_16_out, and_17_out,
       and_18_out, and_19_out, and_20_out, and_21_out, and_22_out, and_23_out, and_24_out, not_1_out,
       not_2_out, not_3_out, not_4_out, not_5_out, not_6_out, not_7_out, not_8_out, not_9_out, not_10_out,
       not_11_out, not_12_out, not_13_out, not_14_out, not_15_out, not_16_out, not_17_out, not_18_out,
       not_19_out, not_20_out, not_21_out, not_22_out, not_23_out, not_24_out, not_25_out, not_26_out,
       not_27_out, not_28_out, not_29_out, not_30_out, not_31_out, not_32_out, not_33_out, not_34_out,
       not_35_out, not_36_out, not_37_out, not_38_out, not_39_out;

  not not_1 (not_1_out, a);
  and and_1 (and_1_out, not_1_out, not_2_out);
  not not_2 (not_2_out, b);
  not not_3 (not_3_out, a);
  and and_2 (and_2_out, not_3_out, not_4_out);
  not not_4 (not_4_out, c);
  not not_5 (not_5_out, b);
  and and_3 (and_3_out, not_5_out, not_6_out);
  not not_6 (not_6_out, c);
  not not_7 (not_7_out, b);
  not not_8 (not_8_out, c);
  not not_9 (not_9_out, d);
  not not_10 (not_10_out, a);
  not not_11 (not_11_out, d);
  not not_12 (not_12_out, a);
  not not_13 (not_13_out, d);
  not not_14 (not_14_out, b);
  and and_4 (and_4_out, not_14_out, not_15_out, d);
  not not_15 (not_15_out, c);
  not not_16 (not_16_out, b);
  and and_5 (and_5_out, a, not_16_out, d);
  not not_17 (not_17_out, b);
  and and_6 (and_6_out, not_17_out, not_18_out, not_19_out);
  not not_18 (not_18_out, c);
  not not_19 (not_19_out, d);
  not not_20 (not_20_out, a);
  and and_7 (and_7_out, not_20_out, b);
  and and_8 (and_8_out, b, c);
  not not_21 (not_21_out, b);
  and and_9 (and_9_out, a, not_21_out, not_22_out);
  not not_22 (not_22_out, d);
  not not_23 (not_23_out, b);
  not not_24 (not_24_out, c);
  and and_10 (and_10_out, not_23_out, not_24_out, not_25_out);
  not not_25 (not_25_out, d);
  not not_26 (not_26_out, a);
  and and_11 (and_11_out, not_26_out, c, d);
  and and_12 (and_12_out, b, d);
  and and_13 (and_13_out, b, c);
  and and_14 (and_14_out, a, not_27_out);
  not not_27 (not_27_out, c);
  and and_15 (and_15_out, a, not_28_out);
  not not_28 (not_28_out, d);
  not not_29 (not_29_out, a);
  not not_30 (not_30_out, a);
  and and_16 (and_16_out, not_30_out, b, c);
  not not_31 (not_31_out, b);
  and and_17 (and_17_out, a, not_31_out, c);
  and and_18 (and_18_out, a, b, not_32_out);
  not not_32 (not_32_out, c);
  and and_19 (and_19_out, a, b, not_33_out);
  not not_33 (not_33_out, d);
  not not_34 (not_34_out, a);
  and and_20 (and_20_out, not_34_out, not_35_out);
  not not_35 (not_35_out, b);
  not not_36 (not_36_out, b);
  and and_21 (and_21_out, not_36_out, d);
  not not_37 (not_37_out, b);
  and and_22 (and_22_out, not_37_out, c);
  and and_23 (and_23_out, b, not_38_out);
  not not_38 (not_38_out, c);
  and and_24 (and_24_out, b, not_39_out);
  not not_39 (not_39_out, d);
  or or_1 (RegDest, and_1_out, and_2_out, and_3_out);
  and and_25 (Branch, a, not_7_out, not_8_out, not_9_out);
  and and_26 (MemRead, not_10_out, b, c, not_11_out);
  and and_27 (MemToReg, not_12_out, b, c, not_13_out);
  or or_2 (ALUOp0, and_4_out, and_5_out);
  or or_3 (ALUOp1, and_6_out, and_7_out, and_8_out, and_9_out);
  and and_28 (MemWrite, not_29_out, b, c, d);
  or or_4 (ALUSrc, and_16_out, and_17_out, and_18_out, and_19_out);
  or or_5 (RegWrite, and_20_out, and_21_out, and_22_out, and_23_out, and_24_out);
  or or_6 (ALUOp2, and_10_out, and_11_out, and_12_out, and_13_out, and_14_out, and_15_out);
endmodule

module CONTROL (
  input  a,
  input  b,
  input  c,
  input  d,
  output RegDest,
  output Branch,
  output MemRead,
  output MemToReg,
  output ALUOp0,
  output ALUOp1,
  output ALUOp2,
  output MemWrite,
  output ALUSrc,
  output RegWrite,
  output Jump
);

  wire and_1_out, and_2_out, and_3_out, and_4_out, and_5_out, and_6_out, and_7_out, and_8_out, and_9_out,
       and_10_out, and_11_out, and_14_out, and_15_out, and_17_out, and_18_out, and_19_out, and_20_out,
       and_21_out, and_22_out, and_23_out, and_24_out, and_26_out, and_27_out, and_28_out, and_29_out,
       not_1_out, not_2_out, not_3_out, not_4_out, not_5_out, not_6_out, not_7_out, not_8_out, not_9_out,
       not_10_out, not_11_out, not_12_out, not_13_out, not_14_out, not_15_out, not_16_out, not_17_out,
       not_18_out, not_19_out, not_20_out, not_21_out, not_22_out, not_23_out, not_24_out, not_25_out,
       not_26_out, not_27_out, not_28_out, not_29_out, not_30_out, not_31_out, not_32_out, not_33_out,
       not_34_out, not_35_out, not_36_out, not_37_out, not_38_out, not_39_out, not_40_out, not_41_out,
       not_42_out, not_43_out, not_44_out, not_45_out, not_46_out, not_47_out;

  not not_1 (not_1_out, a);
  and and_1 (and_1_out, not_1_out, not_2_out);
  not not_2 (not_2_out, b);
  not not_3 (not_3_out, a);
  and and_2 (and_2_out, not_3_out, not_4_out);
  not not_4 (not_4_out, d);
  not not_5 (not_5_out, b);
  not not_6 (not_6_out, c);
  and and_3 (and_3_out, not_5_out, not_6_out, not_7_out);
  not not_7 (not_7_out, d);
  and and_4 (and_4_out, b, c, not_8_out);
  not not_8 (not_8_out, d);
  not not_9 (not_9_out, a);
  not not_10 (not_10_out, a);
  not not_11 (not_11_out, c);
  not not_12 (not_12_out, a);
  not not_13 (not_13_out, d);
  not not_14 (not_14_out, a);
  not not_15 (not_15_out, c);
  not not_16 (not_16_out, a);
  not not_17 (not_17_out, b);
  not not_18 (not_18_out, c);
  not not_19 (not_19_out, a);
  not not_20 (not_20_out, b);
  not not_21 (not_21_out, d);
  not not_22 (not_22_out, a);
  not not_23 (not_23_out, c);
  not not_24 (not_24_out, d);
  not not_25 (not_25_out, a);
  not not_26 (not_26_out, c);
  not not_27 (not_27_out, a);
  not not_28 (not_28_out, d);
  not not_29 (not_29_out, b);
  not not_30 (not_30_out, c);
  not not_31 (not_31_out, b);
  not not_32 (not_32_out, c);
  and and_5 (and_5_out, not_31_out, not_32_out, not_33_out);
  not not_33 (not_33_out, d);
  not not_34 (not_34_out, b);
  and and_6 (and_6_out, not_34_out, c, d);
  not not_35 (not_35_out, c);
  and and_7 (and_7_out, b, not_35_out, d);
  and and_8 (and_8_out, b, c, not_36_out);
  not not_36 (not_36_out, d);
  and and_9 (and_9_out, a, not_37_out);
  not not_37 (not_37_out, c);
  and and_10 (and_10_out, a, b);
  not not_38 (not_38_out, a);
  not not_39 (not_39_out, d);
  not not_40 (not_40_out, c);
  not not_41 (not_41_out, a);
  not not_42 (not_42_out, d);
  not not_43 (not_43_out, b);
  not not_44 (not_44_out, b);
  not not_45 (not_45_out, b);
  not not_46 (not_46_out, c);
  and and_11 (and_11_out, a, not_47_out);
  not not_47 (not_47_out, d);
  and and_12 (Jump, a, b, c, d);
  or or_1 (RegDest, and_1_out, and_2_out, and_3_out, and_4_out);
  and and_13 (Branch, not_9_out, b, c, d);
  and and_14 (and_14_out, not_10_out, b, not_11_out, d);
  or or_2 (MemRead, and_14_out, and_15_out);
  and and_15 (and_15_out, not_12_out, b, c, not_13_out);
  and and_16 (MemToReg, not_14_out, b, not_15_out, d);
  and and_17 (and_17_out, not_16_out, not_17_out, not_18_out, d);
  or or_3 (ALUOp0, and_17_out, and_18_out, and_19_out);
  and and_18 (and_18_out, not_19_out, b, c, d);
  and and_19 (and_19_out, a, not_20_out, not_21_out);
  and and_20 (and_20_out, not_22_out, not_23_out, not_24_out);
  and and_21 (and_21_out, not_25_out, b, not_26_out);
  and and_22 (and_22_out, not_27_out, b, not_28_out);
  and and_23 (and_23_out, a, not_29_out, not_30_out, d);
  and and_24 (and_24_out, a, b, c);
  and and_25 (MemWrite, not_38_out, b, c, not_39_out);
  and and_26 (and_26_out, b, not_40_out, d);
  and and_27 (and_27_out, not_41_out, b, c, not_42_out);
  and and_28 (and_28_out, a, not_43_out, d);
  and and_29 (and_29_out, a, not_44_out, c);
  or or_4 (RegWrite, not_45_out, not_46_out, and_11_out);
  or or_5 (ALUOp1, and_20_out, and_21_out, and_22_out, and_23_out, and_24_out);
  or or_6 (ALUOp2, and_5_out, and_6_out, and_7_out, and_8_out, and_9_out, and_10_out);
  or or_7 (ALUSrc, and_26_out, and_27_out, and_28_out, and_29_out);
endmodule
